# Fritzing sketch sensor-hardware (saved by Fritzing 0.9.3b)
circuit board: 6.25936cm x 3.60458cm
stripboards: 1

parts:
  Arduino_Micro = Arduino Micro (Rev3)
  R2 = Resistor [tolerance=±5% resistance=120 package=THT]
  SF_4346 = LED - 5mm [color="Infrared (940nm)" package="5 mm [THT]"]
  R3 = Resistor [tolerance=±5% resistance=2.2k package=THT]
  SF_309_FA = LTR-301 [package=ltr-301]
  LED1 = LED - 5mm [color="Green (555nm)" package="5 mm [THT]"]
  R1 = Resistor [tolerance=±5% resistance=220 package=THT]

nets:
  GND: Arduino_Micro.GND, R2.Pin_0, R3.Pin_1, R1.Pin_1
  N1: Arduino_Micro.D2/SDA, SF_4346.cathode
  N2: Arduino_Micro.D12_PWM/A11, LED1.anode
  5V: Arduino_Micro.5V, SF_309_FA.C
  N3: Arduino_Micro.A0, R3.Pin_0, SF_309_FA.E
  N4: R2.Pin_1, SF_4346.anode
  N5: LED1.cathode, R1.Pin_0
